// Logisim project one_bit_adder.circ as structural Verilog: 14 circuits, main circuit one_bit_adder
module one_bit_adder (
  input  A,
  input  B,
  input  C_In,
  output S,
  output C_Out
);

  wire and_1_out, and_2_out, and_3_out, and_4_out, and_5_out, and_6_out, and_7_out, not_1_out, not_2_out,
       not_3_out, not_4_out, not_5_out, not_6_out;

  not not_1 (not_1_out, A);
  not not_2 (not_2_out, B);
  not not_3 (not_3_out, A);
  not not_4 (not_4_out, C_In);
  not not_5 (not_5_out, B);
  not not_6 (not_6_out, C_In);
  and and_1 (and_1_out, not_1_out, not_2_out, C_In);
  and and_2 (and_2_out, not_3_out, B, not_4_out);
  and and_3 (and_3_out, A, not_5_out, not_6_out);
  and and_4 (and_4_out, A, B, C_In);
  and and_5 (and_5_out, B, A);
  and and_6 (and_6_out, A, C_In);
  and and_7 (and_7_out, A, B);
  or or_1 (S, and_1_out, and_2_out, and_3_out, and_4_out);
  or or_2 (C_Out, and_5_out, and_6_out, and_7_out);
endmodule

module one_bit_ALU (
  input  [3:0] ALU_Ctrl,
  input  A,
  input  B,
  input  C_In,
  output R,
  output C_Out
);

  wire and_1_out, multiplexer_1_out, not_1_out, one_bit_adder_1_s, or_1_out, xor_1_out;

  not not_1 (not_1_out, B);
  Multiplexer #(.enable("false")) multiplexer_1 (.in0(B), .in1(not_1_out), .out(multiplexer_1_out), .sel(ALU_Ctrl[2]));
  and and_1 (and_1_out, A, multiplexer_1_out);
  or or_1 (or_1_out, A, multiplexer_1_out);
  xor xor_1 (xor_1_out, A, multiplexer_1_out);
  one_bit_adder one_bit_adder_1 (.A(A), .B(multiplexer_1_out), .C_In(C_In), .S(one_bit_adder_1_s), .C_Out(C_Out));
  Multiplexer #(.enable("false"), .select(2)) multiplexer_2 (
    .in0(and_1_out), .in1(or_1_out), .in2(xor_1_out), .in3(one_bit_adder_1_s), .out(R), .sel(ALU_Ctrl[1:0]));
endmodule

module ALU_Control (
  input  L_30,
  input  L_14,
  input  L_13,
  input  L_12,
  input  L_6,
  input  L_5,
  input  L_4,
  output ALU_Ctrl_3,
  output ALU_Ctrl_2,
  output ALU_Ctrl_1,
  output ALU_Ctrl_0,
  output ALU_Src
);

  wire and_2_out, not_1_out, not_2_out, not_3_out, not_4_out, not_5_out;

  not not_1 (not_1_out, L_14);
  not not_2 (not_2_out, L_13);
  not not_3 (not_3_out, L_12);
  not not_4 (not_4_out, L_5);
  not not_5 (not_5_out, L_4);
  and and_1 (ALU_Ctrl_2, L_30, not_2_out, L_5);
  or or_1 (ALU_Ctrl_1, not_2_out, not_5_out);
  and and_2 (and_2_out, L_13, not_3_out);
  or or_2 (ALU_Src, not_4_out, not_5_out);
  or or_3 (ALU_Ctrl_0, not_1_out, and_2_out);

  assign ALU_Ctrl_3 = 1'b0;
endmodule

module ALU_4Bit (
  input  [3:0] ALU_Ctrl,
  input  [3:0] A,
  input  [3:0] B,
  input  C_In,
  output [3:0] R,
  output C_Out
);

  wire one_bit_alu_1_c_out, one_bit_alu_2_c_out, one_bit_alu_3_c_out;

  one_bit_ALU one_bit_alu_1 (
    .ALU_Ctrl(ALU_Ctrl), .A(A[0]), .B(B[0]), .C_In(C_In), .R(R[0]), .C_Out(one_bit_alu_1_c_out));
  one_bit_ALU one_bit_alu_2 (
    .ALU_Ctrl(ALU_Ctrl), .A(A[1]), .B(B[1]), .C_In(one_bit_alu_1_c_out), .R(R[1]), .C_Out(one_bit_alu_2_c_out));
  one_bit_ALU one_bit_alu_3 (
    .ALU_Ctrl(ALU_Ctrl), .A(A[2]), .B(B[2]), .C_In(one_bit_alu_2_c_out), .R(R[2]), .C_Out(one_bit_alu_3_c_out));
  one_bit_ALU one_bit_alu_4 (
    .ALU_Ctrl(ALU_Ctrl), .A(A[3]), .B(B[3]), .C_In(one_bit_alu_3_c_out), .R(R[3]), .C_Out(C_Out));
endmodule

module ALU_32Bit (
  input  [3:0] ALU_Ctrl,
  input  [31:0] A,
  input  [31:0] B,
  output [31:0] Result,
  output C_Out
);

  wire alu_4bit_1_c_out, alu_4bit_2_c_out, alu_4bit_3_c_out, alu_4bit_4_c_out, alu_4bit_5_c_out,
       alu_4bit_6_c_out, alu_4bit_7_c_out;

  ALU_4Bit alu_4bit_1 (
    .ALU_Ctrl(ALU_Ctrl), .A(A[3:0]), .B(B[3:0]), .C_In(ALU_Ctrl[2]), .R(Result[3:0]), .C_Out(alu_4bit_1_c_out));
  ALU_4Bit alu_4bit_2 (
    .ALU_Ctrl(ALU_Ctrl), .A(A[7:4]), .B(B[7:4]), .C_In(alu_4bit_1_c_out), .R(Result[7:4]),
    .C_Out(alu_4bit_2_c_out));
  ALU_4Bit alu_4bit_3 (
    .ALU_Ctrl(ALU_Ctrl), .A(A[11:8]), .B(B[11:8]), .C_In(alu_4bit_2_c_out), .R(Result[11:8]),
    .C_Out(alu_4bit_3_c_out));
  ALU_4Bit alu_4bit_4 (
    .ALU_Ctrl(ALU_Ctrl), .A(A[15:12]), .B(B[15:12]), .C_In(alu_4bit_3_c_out), .R(Result[15:12]),
    .C_Out(alu_4bit_4_c_out));
  ALU_4Bit alu_4bit_5 (
    .ALU_Ctrl(ALU_Ctrl), .A(A[19:16]), .B(B[19:16]), .C_In(alu_4bit_4_c_out), .R(Result[19:16]),
    .C_Out(alu_4bit_5_c_out));
  ALU_4Bit alu_4bit_6 (
    .ALU_Ctrl(ALU_Ctrl), .A(A[23:20]), .B(B[23:20]), .C_In(alu_4bit_5_c_out), .R(Result[23:20]),
    .C_Out(alu_4bit_6_c_out));
  ALU_4Bit alu_4bit_7 (
    .ALU_Ctrl(ALU_Ctrl), .A(A[27:24]), .B(B[27:24]), .C_In(alu_4bit_6_c_out), .R(Result[27:24]),
    .C_Out(alu_4bit_7_c_out));
  ALU_4Bit alu_4bit_8 (
    .ALU_Ctrl(ALU_Ctrl), .A(A[31:28]), .B(B[31:28]), .C_In(alu_4bit_7_c_out), .R(Result[31:28]), .C_Out(C_Out));
endmodule

module RegisterFile0 (
  input  [1:0] RReg1,
  input  [1:0] RReg2,
  input  [31:0] WData,
  input  Clock_In,
  input  Write,
  input  [1:0] WReg,
  output [31:0] out_7,
  output [31:0] out_8
);

  wire demultiplexer_1_out0, demultiplexer_1_out1, demultiplexer_1_out2, demultiplexer_1_out3;
  wire [31:0] register_1_q, register_2_q, register_3_q, register_4_q;

  Demultiplexer #(.enable("false"), .select(2)) demultiplexer_1 (
    .out0(demultiplexer_1_out0), .out1(demultiplexer_1_out1), .out2(demultiplexer_1_out2),
    .out3(demultiplexer_1_out3), .in(Write), .sel(WReg));
  Register #(.width(32)) register_1 (
    .D(WData), .en(demultiplexer_1_out0), .clk(Clock_In), .Q(register_1_q), .clr(Write));
  Register #(.width(32)) register_2 (
    .D(WData), .en(demultiplexer_1_out1), .clk(Clock_In), .Q(register_2_q));  // open: clr
  Register #(.width(32)) register_3 (
    .D(WData), .en(demultiplexer_1_out2), .clk(Clock_In), .Q(register_3_q));  // open: clr
  Register #(.width(32)) register_4 (
    .D(WData), .en(demultiplexer_1_out3), .clk(Clock_In), .Q(register_4_q));  // open: clr
  Multiplexer #(.enable("false"), .select(2), .width(32)) multiplexer_1 (
    .in0(register_1_q), .in1(register_2_q), .in2(register_3_q), .in3(register_4_q), .out(out_7), .sel(RReg1));
  Multiplexer #(.enable("false"), .select(2), .width(32)) multiplexer_2 (
    .in0(register_1_q), .in1(register_2_q), .in2(register_3_q), .in3(register_4_q), .out(out_8), .sel(RReg2));
endmodule

module RegisterFile32 (
  input  [1:0] RReg1,
  input  [1:0] RReg2,
  input  [31:0] WData,
  input  Clock_In,
  input  Write,
  input  [1:0] WReg,
  output [31:0] out_7,
  output [31:0] out_8
);

  wire demultiplexer_1_out0, demultiplexer_1_out1, demultiplexer_1_out2, demultiplexer_1_out3;
  wire [31:0] register_1_q, register_2_q, register_3_q, register_4_q;

  Demultiplexer #(.enable("false"), .select(2)) demultiplexer_1 (
    .out0(demultiplexer_1_out0), .out1(demultiplexer_1_out1), .out2(demultiplexer_1_out2),
    .out3(demultiplexer_1_out3), .in(Write), .sel(WReg));
  Register #(.width(32)) register_1 (
    .D(WData), .en(demultiplexer_1_out0), .clk(Clock_In), .Q(register_1_q));  // open: clr
  Register #(.width(32)) register_2 (
    .D(WData), .en(demultiplexer_1_out1), .clk(Clock_In), .Q(register_2_q));  // open: clr
  Register #(.width(32)) register_3 (
    .D(WData), .en(demultiplexer_1_out2), .clk(Clock_In), .Q(register_3_q));  // open: clr
  Register #(.width(32)) register_4 (
    .D(WData), .en(demultiplexer_1_out3), .clk(Clock_In), .Q(register_4_q));  // open: clr
  Multiplexer #(.enable("false"), .select(2), .width(32)) multiplexer_1 (
    .in0(register_1_q), .in1(register_2_q), .in2(register_3_q), .in3(register_4_q), .out(out_7), .sel(RReg1));
  Multiplexer #(.enable("false"), .select(2), .width(32)) multiplexer_2 (
    .in0(register_1_q), .in1(register_2_q), .in2(register_3_q), .in3(register_4_q), .out(out_8), .sel(RReg2));
endmodule

module RegisterFile3232 (
  input  [4:0] RReg1,
  input  [4:0] RReg2,
  input  Clock_In,
  input  [31:0] WData,
  input  Write,
  input  [4:0] WReg,
  output [31:0] RData1,
  output [31:0] RData2
);

  wire demultiplexer_1_out0, demultiplexer_1_out1, demultiplexer_1_out2, demultiplexer_1_out3,
       demultiplexer_1_out4, demultiplexer_1_out5, demultiplexer_1_out6, demultiplexer_1_out7;
  wire [31:0] registerfile0_1_out_7, registerfile0_1_out_8, registerfile32_1_out_7, registerfile32_1_out_8,
       registerfile32_2_out_7, registerfile32_2_out_8, registerfile32_3_out_7, registerfile32_3_out_8,
       registerfile32_4_out_7, registerfile32_4_out_8, registerfile32_5_out_7, registerfile32_5_out_8,
       registerfile32_6_out_7, registerfile32_6_out_8, registerfile32_7_out_7, registerfile32_7_out_8;

  Demultiplexer #(.enable("false"), .select(3)) demultiplexer_1 (
    .out0(demultiplexer_1_out0), .out1(demultiplexer_1_out1), .out2(demultiplexer_1_out2),
    .out3(demultiplexer_1_out3), .out4(demultiplexer_1_out4), .out5(demultiplexer_1_out5),
    .out6(demultiplexer_1_out6), .out7(demultiplexer_1_out7), .in(Write), .sel(WReg[4:2]));
  RegisterFile0 registerfile0_1 (
    .RReg1(RReg1[1:0]), .RReg2(RReg2[1:0]), .WData(WData), .Clock_In(Clock_In), .Write(demultiplexer_1_out0),
    .WReg(WReg[1:0]), .out_7(registerfile0_1_out_7), .out_8(registerfile0_1_out_8));
  RegisterFile32 registerfile32_1 (
    .RReg1(RReg1[1:0]), .RReg2(RReg2[1:0]), .WData(WData), .Clock_In(Clock_In), .Write(demultiplexer_1_out1),
    .WReg(WReg[1:0]), .out_7(registerfile32_1_out_7), .out_8(registerfile32_1_out_8));
  RegisterFile32 registerfile32_2 (
    .RReg1(RReg1[1:0]), .RReg2(RReg2[1:0]), .WData(WData), .Clock_In(Clock_In), .Write(demultiplexer_1_out2),
    .WReg(WReg[1:0]), .out_7(registerfile32_2_out_7), .out_8(registerfile32_2_out_8));
  RegisterFile32 registerfile32_3 (
    .RReg1(RReg1[1:0]), .RReg2(RReg2[1:0]), .WData(WData), .Clock_In(Clock_In), .Write(demultiplexer_1_out3),
    .WReg(WReg[1:0]), .out_7(registerfile32_3_out_7), .out_8(registerfile32_3_out_8));
  RegisterFile32 registerfile32_4 (
    .RReg1(RReg1[1:0]), .RReg2(RReg2[1:0]), .WData(WData), .Clock_In(Clock_In), .Write(demultiplexer_1_out4),
    .WReg(WReg[1:0]), .out_7(registerfile32_4_out_7), .out_8(registerfile32_4_out_8));
  RegisterFile32 registerfile32_5 (
    .RReg1(RReg1[1:0]), .RReg2(RReg2[1:0]), .WData(WData), .Clock_In(Clock_In), .Write(demultiplexer_1_out5),
    .WReg(WReg[1:0]), .out_7(registerfile32_5_out_7), .out_8(registerfile32_5_out_8));
  RegisterFile32 registerfile32_6 (
    .RReg1(RReg1[1:0]), .RReg2(RReg2[1:0]), .WData(WData), .Clock_In(Clock_In), .Write(demultiplexer_1_out6),
    .WReg(WReg[1:0]), .out_7(registerfile32_6_out_7), .out_8(registerfile32_6_out_8));
  RegisterFile32 registerfile32_7 (
    .RReg1(RReg1[1:0]), .RReg2(RReg2[1:0]), .WData(WData), .Clock_In(Clock_In), .Write(demultiplexer_1_out7),
    .WReg(WReg[1:0]), .out_7(registerfile32_7_out_7), .out_8(registerfile32_7_out_8));
  Multiplexer #(.enable("false"), .select(3), .width(32)) multiplexer_1 (
    .in0(registerfile0_1_out_7), .in1(registerfile32_1_out_7), .in2(registerfile32_2_out_7),
    .in3(registerfile32_3_out_7), .in4(registerfile32_4_out_7), .in5(registerfile32_5_out_7),
    .in6(registerfile32_6_out_7), .in7(registerfile32_7_out_7), .out(RData1), .sel(RReg1[4:2]));
  Multiplexer #(.enable("false"), .select(3), .width(32)) multiplexer_2 (
    .in0(registerfile0_1_out_8), .in1(registerfile32_1_out_8), .in2(registerfile32_2_out_8),
    .in3(registerfile32_3_out_8), .in4(registerfile32_4_out_8), .in5(registerfile32_5_out_8),
    .in6(registerfile32_6_out_8), .in7(registerfile32_7_out_8), .out(RData2), .sel(RReg2[4:2]));
endmodule

module CompletedCircuit (
  input  [31:0] Instruction
);

  wire alu_control_1_alu_src, clock_1_out;
  wire [3:0] alu_control_1_alu_ctrl_0;
  wire [31:0] alu_32bit_1_result, bit_extender_1_out, multiplexer_1_out, registerfile3232_1_rdata1,
       registerfile3232_1_rdata2;

  Clock clock_1 (.out(clock_1_out));
  assign bit_extender_1_out = {{20{Instruction[31]}}, Instruction[31:20]};  // Bit_Extender bit_extender_1
  RegisterFile3232 registerfile3232_1 (
    .RReg1(Instruction[19:15]), .RReg2(Instruction[24:20]), .Clock_In(clock_1_out),
    .WData(alu_32bit_1_result), .Write(1'b1), .WReg(Instruction[11:7]), .RData1(registerfile3232_1_rdata1),
    .RData2(registerfile3232_1_rdata2));
  ALU_Control alu_control_1 (
    .L_30(Instruction[30]), .L_14(Instruction[14]), .L_13(Instruction[13]), .L_12(Instruction[12]),
    .L_6(Instruction[6]), .L_5(Instruction[5]), .L_4(Instruction[4]),
    .ALU_Ctrl_3(alu_control_1_alu_ctrl_0[3]), .ALU_Ctrl_2(alu_control_1_alu_ctrl_0[2]),
    .ALU_Ctrl_1(alu_control_1_alu_ctrl_0[1]), .ALU_Ctrl_0(alu_control_1_alu_ctrl_0[0]),
    .ALU_Src(alu_control_1_alu_src));
  Multiplexer #(.enable("false"), .width(32)) multiplexer_1 (
    .in0(registerfile3232_1_rdata2), .in1(bit_extender_1_out), .out(multiplexer_1_out),
    .sel(alu_control_1_alu_src));
  ALU_32Bit alu_32bit_1 (
    .ALU_Ctrl(alu_control_1_alu_ctrl_0), .A(registerfile3232_1_rdata1), .B(multiplexer_1_out),
    .Result(alu_32bit_1_result));  // open: C_Out
endmodule

module ImmGen32 (
  input  [31:0] Instruction,
  output [31:0] IMM32
);

  Multiplexer #(.enable("false"), .width(4)) multiplexer_1 (
    .in0(Instruction[24:21]), .in1(Instruction[11:8]), .out(IMM32[4:1]), .sel(Instruction[5]));
  Multiplexer #(.enable("false")) multiplexer_2 (
    .in0(Instruction[31]), .in1(Instruction[7]), .out(IMM32[11]), .sel(Instruction[6]));
  assign IMM32[31:12] = {{19{Instruction[31]}}, Instruction[31]};  // Bit_Extender bit_extender_1
  Multiplexer #(.enable("false"), .select(2)) multiplexer_3 (
    .in0(Instruction[20]), .in1(Instruction[7]), .in3(1'b0), .out(IMM32[0]), .sel(Instruction[6:5]));  // open: in2

  assign IMM32[10:5] = Instruction[30:25];

  // Other names for the same wires on the sheet: I30_25[5:0] = Instruction[30:25]; I5 = Instruction[5];
  //   I6_5[1:0] = Instruction[6:5]; I6 = Instruction[6]; I7 = Instruction[7]; I11_8[3:0] = Instruction[11:8];
  //   I_20 = Instruction[20]; I24_21[3:0] = Instruction[24:21]; I31 = Instruction[31]
endmodule

module MainControlCircuit (
  input  [6:0] I6_0,
  output MemToReg,
  output RegWrite,
  output MemRead,
  output MemWrite,
  output Branch
);

  wire not_1_out, not_2_out;

  not not_1 (not_1_out, I6_0[6]);
  not not_2 (not_2_out, I6_0[5]);
  not not_3 (MemToReg, I6_0[4]);
  or or_1 (RegWrite, not_2_out, I6_0[4]);
  and and_1 (MemRead, not_2_out, MemToReg);
  and and_2 (MemWrite, not_1_out, I6_0[5], MemToReg);

  assign Branch = I6_0[6];
endmodule

module InstructionMemory (
  input  [23:0] Address,
  input  ClockIn,
  output [31:0] Instruction
);

  wire not_1_out;

  not not_1 (not_1_out, ClockIn);
  RAM #(.addrWidth(22), .asyncread("true"), .dataWidth(32)) ram_1 (
    .addr(Address[23:2]), .we(1'b0), .oe(not_1_out), .dout(Instruction));  // open: clk, din
endmodule

module DataMemory (
  input  [25:0] Address,
  input  MemWrite,
  input  MemRead,
  input  ClockIn,
  input  [31:0] WriteData,
  output [31:0] ReadData
);

  RAM #(.addrWidth(24), .asyncread("true"), .dataWidth(32)) ram_1 (
    .addr(Address[25:2]), .we(MemWrite), .oe(MemRead), .clk(ClockIn), .din(WriteData), .dout(ReadData));
endmodule

module CompletedCircuit2 (
);

  wire alu_control_1_alu_src, and_1_out, clock_1_out, comparator_1_eq, maincontrolcircuit_1_branch,
       maincontrolcircuit_1_memread, maincontrolcircuit_1_memtoreg, maincontrolcircuit_1_memwrite,
       maincontrolcircuit_1_regwrite;
  wire [3:0] alu_control_1_alu_ctrl_0;
  wire [7:0] register_1_q_2;
  wire [23:0] register_1_q;
  wire [31:0] adder_1_out, adder_2_out, alu_32bit_1_result, datamemory_1_readdata, immgen32_1_imm32,
       instructionmemory_1_instruction, multiplexer_1_out, multiplexer_2_out, multiplexer_3_out,
       registerfile3232_1_rdata1, registerfile3232_1_rdata2;

  Register #(.width(32)) register_1 (
    .D(multiplexer_2_out), .en(1'b1), .clk(clock_1_out), .Q({register_1_q_2, register_1_q}));  // open: clr
  Clock clock_1 (.out(clock_1_out));
  Adder #(.width(32)) adder_1 (.a({register_1_q_2, register_1_q}), .b(32'h4), .out(adder_1_out));  // open: cin, cout
  InstructionMemory instructionmemory_1 (
    .Address(register_1_q), .ClockIn(clock_1_out), .Instruction(instructionmemory_1_instruction));
  ImmGen32 immgen32_1 (.Instruction(instructionmemory_1_instruction), .IMM32(immgen32_1_imm32));
  RegisterFile3232 registerfile3232_1 (
    .RReg1(instructionmemory_1_instruction[19:15]), .RReg2(instructionmemory_1_instruction[24:20]),
    .Clock_In(clock_1_out), .WData(multiplexer_3_out), .Write(maincontrolcircuit_1_regwrite),
    .WReg(instructionmemory_1_instruction[11:7]), .RData1(registerfile3232_1_rdata1),
    .RData2(registerfile3232_1_rdata2));
  MainControlCircuit maincontrolcircuit_1 (
    .I6_0(instructionmemory_1_instruction[6:0]), .MemToReg(maincontrolcircuit_1_memtoreg),
    .RegWrite(maincontrolcircuit_1_regwrite), .MemRead(maincontrolcircuit_1_memread),
    .MemWrite(maincontrolcircuit_1_memwrite), .Branch(maincontrolcircuit_1_branch));
  Multiplexer #(.enable("false"), .width(32)) multiplexer_1 (
    .in0(registerfile3232_1_rdata2), .in1(immgen32_1_imm32), .out(multiplexer_1_out),
    .sel(alu_control_1_alu_src));
  ALU_Control alu_control_1 (
    .L_30(instructionmemory_1_instruction[31]), .L_14(instructionmemory_1_instruction[14]),
    .L_13(instructionmemory_1_instruction[13]), .L_12(instructionmemory_1_instruction[12]),
    .L_6(instructionmemory_1_instruction[6]), .L_5(instructionmemory_1_instruction[5]),
    .L_4(instructionmemory_1_instruction[4]), .ALU_Ctrl_3(alu_control_1_alu_ctrl_0[3]),
    .ALU_Ctrl_2(alu_control_1_alu_ctrl_0[2]), .ALU_Ctrl_1(alu_control_1_alu_ctrl_0[1]),
    .ALU_Ctrl_0(alu_control_1_alu_ctrl_0[0]), .ALU_Src(alu_control_1_alu_src));
  Comparator #(.width(32)) comparator_1 (
    .a(registerfile3232_1_rdata1), .b(registerfile3232_1_rdata2), .eq(comparator_1_eq));  // open: gt, lt
  ALU_32Bit alu_32bit_1 (
    .ALU_Ctrl(alu_control_1_alu_ctrl_0), .A(registerfile3232_1_rdata1), .B(multiplexer_1_out),
    .Result(alu_32bit_1_result));  // open: C_Out
  Adder #(.width(32)) adder_2 (
    .a({register_1_q_2, register_1_q}), .b(immgen32_1_imm32), .out(adder_2_out));  // open: cin, cout
  and and_1 (and_1_out, maincontrolcircuit_1_branch, comparator_1_eq);
  Multiplexer #(.enable("false"), .width(32)) multiplexer_2 (
    .in0(adder_1_out), .in1(adder_2_out), .out(multiplexer_2_out), .sel(and_1_out));
  DataMemory datamemory_1 (
    .Address(alu_32bit_1_result[25:0]), .MemWrite(maincontrolcircuit_1_memwrite),
    .MemRead(maincontrolcircuit_1_memread), .ClockIn(clock_1_out), .WriteData(registerfile3232_1_rdata2),
    .ReadData(datamemory_1_readdata));
  Multiplexer #(.enable("false"), .width(32)) multiplexer_3 (
    .in0(alu_32bit_1_result), .in1(datamemory_1_readdata), .out(multiplexer_3_out),
    .sel(maincontrolcircuit_1_memtoreg));
endmodule
